// Digital circuit Dilemme.dig as structural Verilog
module Dilemme (
  input  A,
  input  B,
  output S
);

  wire and_1_out, and_2_out, and_3_out, and_4_out, not_1_out, not_2_out, not_3_out;

  and and_1 (and_1_out, A, B);
  not not_1 (not_1_out, and_1_out);
  and and_2 (and_2_out, A, not_1_out);
  and and_3 (and_3_out, not_1_out, B);
  not not_2 (not_2_out, and_2_out);
  not not_3 (not_3_out, and_3_out);
  and and_4 (and_4_out, not_2_out, not_3_out);
  not not_4 (S, and_4_out);
endmodule
