// Digital circuit fullAdder.dig as structural Verilog
module fullAdder (
  input  Ai,
  input  Bi,
  input  Ri_1,
  output Si,
  output Ri
);

  wire halfadder_1_r, halfadder_1_s, halfadder_2_r;

  halfAdder halfadder_1 (.A(Ai), .B(Bi), .S(halfadder_1_s), .R(halfadder_1_r));
  halfAdder halfadder_2 (.A(halfadder_1_s), .B(Ri_1), .S(Si), .R(halfadder_2_r));
  or or_1 (Ri, halfadder_2_r, halfadder_1_r);
endmodule
