// Digital circuit mux1.dig as structural Verilog
module mux1 (
  input  A0,
  input  A1,
  input  A2,
  input  A3,
  input  [1:0] Select,
  output S
);

  Multiplexer #(.Selector_Bits(2)) multiplexer_1 (.sel(Select), .in_0(A0), .in_1(A1), .in_2(A2), .in_3(A3), .out(S));
endmodule
