// Digital circuit test_mux.dig as structural Verilog
module test_mux (
  input  Ad0,
  input  Ad1,
  input  [1:0] A0,
  input  [1:0] A1,
  input  [1:0] A2,
  input  [1:0] A3,
  output [1:0] S
);

  Multiplexer #(.Bits(2), .Selector_Bits(2)) multiplexer_1 (
    .sel({Ad1, Ad0}), .in_0(A0), .in_1(A1), .in_2(A2), .in_3(A3), .out(S));
  // Pins of 1 and 2 bits meet at A0
  // Pins of 1 and 2 bits meet at A1
  // Pins of 1 and 2 bits meet at A2
  // Pins of 1 and 2 bits meet at A3
  // Pins of 1 and 2 bits meet at S
endmodule
